// Logisim project MIPS-Lite-吴天鹤18021006.circ as structural Verilog: 11 circuits, main circuit 18021006_Main_Circuit
module _18021006_Main_Circuit (
  input  reset
);

  wire ALUSrc, clk, jsel, MemtoReg, MemWrite, nPC_sel, RegDst, RegWrite, zero;
  wire [1:0] Extop;
  wire [2:0] ALUctr;
  wire [4:0] multiplexer_1_out;
  wire [5:0] n18021006_ifu_1_instruction;
  wire [25:0] j26;
  wire [31:0] busW, multiplexer_2_out, n18021006_alu_1_out, n18021006_dm_1_out, n18021006_ext_1_output32,
       n18021006_gpr_1_busa, n18021006_gpr_1_busb;

  // Probe on j26[5:0]
  // Probe on n18021006_ifu_1_instruction
  _18021006_IFU u_18021006_ifu_1 (
    .clk(clk), .reset(reset), .npc_sel(nPC_sel), .jsel(jsel), .zero(zero),
    .Instruction({n18021006_ifu_1_instruction, j26}), .j26(j26));
  _18021006_Controller u_18021006_controller_1 (
    .opcode(n18021006_ifu_1_instruction), .funct(j26[5:0]), .RegDst(RegDst), .ALUSrc(ALUSrc),
    .MemtoReg(MemtoReg), .RegWrite(RegWrite), .MemWrite(MemWrite), .nPC_sel(nPC_sel), .Extop(Extop),
    .jsel(jsel), .ALUctr(ALUctr));
  Multiplexer #(.select(1), .width(5), .disabled("Z"), .enable("false")) multiplexer_1 (
    .in0(j26[20:16]), .in1(j26[15:11]), .out(multiplexer_1_out), .sel(RegDst));
  _18021006_GPR u_18021006_gpr_1 (
    .busW(busW), .RegWr(RegWrite), .rw(multiplexer_1_out), .ra(j26[25:21]), .rb(j26[20:16]),
    .busA(n18021006_gpr_1_busa), .busB(n18021006_gpr_1_busb), .Clk(clk), .Reset(reset));
  _18021006_EXT u_18021006_ext_1 (.Input_Imm16(j26[15:0]), .ExtOp(Extop), .Output32(n18021006_ext_1_output32));
  Multiplexer #(.select(1), .width(32), .disabled("Z"), .enable("false")) multiplexer_2 (
    .in0(n18021006_gpr_1_busb), .in1(n18021006_ext_1_output32), .out(multiplexer_2_out), .sel(ALUSrc));
  _18021006_ALU u_18021006_alu_1 (
    .busA(n18021006_gpr_1_busa), .busB(multiplexer_2_out), .out(n18021006_alu_1_out), .ALUctr(ALUctr),
    .zero(zero));
  Clock #(.highDuration(1), .lowDuration(1)) u_clk (.out(clk));
  // Probe on n18021006_alu_1_out
  _18021006_DM u_18021006_dm_1 (
    .busA(n18021006_alu_1_out), .busB(n18021006_gpr_1_busb), .Out(n18021006_dm_1_out), .Clk(clk),
    .MemWr(MemWrite));
  Multiplexer #(.select(1), .width(32), .disabled("Z"), .enable("false")) multiplexer_3 (
    .in0(n18021006_alu_1_out), .in1(n18021006_dm_1_out), .out(busW), .sel(MemtoReg));
endmodule

// 18021006 IFU
module _18021006_IFU (
  input  clk,
  input  reset,
  input  npc_sel,
  input  jsel,
  input  zero,
  input  [25:0] j26,
  output [31:0] Instruction
);

  wire [0:0] and_1_out;
  wire [31:0] adder_2_out, bit_extender_1_out, j, multiplexer_1_out, PC_q, shifter_1_out;

  assign bit_extender_1_out = {{16{Instruction[15]}}, Instruction[15:0]};  // Bit_Extender bit_extender_1
  and and_1 (and_1_out[0], npc_sel, zero);
  Shifter #(.width(32), .shift("ll")) shifter_1 (.in(bit_extender_1_out), .\dist (5'b00010), .out(shifter_1_out));
  Adder #(.width(32)) adder_1 (.a(PC_q), .b(32'h4), .out(j));  // open: cin, cout
  Adder #(.width(32)) adder_2 (.a(j), .b(shifter_1_out), .out(adder_2_out));  // open: cin, cout
  Multiplexer #(.select(2), .width(32), .disabled("Z"), .enable("false")) multiplexer_1 (
    .in0(j), .in1(adder_2_out), .in2({j[31:28], j26, 2'b00}), .out(multiplexer_1_out),
    .sel({jsel, and_1_out[0]}));  // open: in3
  Register #(.width(32), .trigger("rising"), .Select("low")) PC (
    .D(multiplexer_1_out), .Q(PC_q), .clk(clk), .clr(reset));  // open: en
  ROM #(.addrWidth(8), .dataWidth(8), .Select("low")) ROM_0 (.addr(PC_q[9:2]), .data(Instruction[31:24]));
  ROM #(.addrWidth(8), .dataWidth(8), .Select("low")) ROM_1 (.addr(PC_q[9:2]), .data(Instruction[23:16]));
  ROM #(.addrWidth(8), .dataWidth(8), .Select("low")) ROM_2 (.addr(PC_q[9:2]), .data(Instruction[15:8]));
  ROM #(.addrWidth(8), .dataWidth(8), .Select("low")) ROM_3 (.addr(PC_q[9:2]), .data(Instruction[7:0]));
  // Probe on Instruction

  // Other names for the same wires on the sheet: imm[15:0] = Instruction[15:0]

  // Notes on the sheet:
  //   contents of ROM_0 (hex, n*v repeats v):
  //   5*34 2 2 10 0 8 ac ac 0 10 8 2 2 8c 8c 36 36 3c 3c
  //   contents of ROM_1 (hex, n*v repeats v):
  //   21 42 63 84 a5 83 a4 65 c3 0 3 4 83 64 0 b4 b4 f 10 31 52 11 12
  //   contents of ROM_2 (hex, n*v repeats v):
  //   10 1 0 0 0 a0 a8 0 30 c 0 0 20 0 c a8 a8 0 0 11 ab ab cd
  //   contents of ROM_3 (hex, n*v repeats v):
  //   10 1 a 64 a 21 21 2 21 c 4 c 23 1 c 23 23 4 c 11 cd ab cd
endmodule

// 18021006 GPR
module _18021006_GPR (
  input  Reset,
  input  Clk,
  input  [31:0] busW,
  input  RegWr,
  input  [4:0] rw,
  input  [4:0] ra,
  input  [4:0] rb,
  output [31:0] busA,
  output [31:0] busB
);

  wire S0, S1, S2, S3, S4, S5, S6, S7, S8, S9, S10, S11, S12, S13, S14, S15, S16, S17, S18, S19, S20, S21,
       S22, S23, S24, S25, S26, S27, S28, S29, S30, S31;
  wire [31:0] _0, _1, _2, _3, _4, _5, _6, _7, _8, _9, _10, _11, _12, _13, _14, _15, _16, _17, _18, _19, _20,
       _21, _22, _23, _24, _25, _26, _27, _28, _29, _30, _31;

  Demultiplexer #(.select(5), .width(1), .tristate("false"), .disabled("Z"), .enable("false")) demultiplexer_1 (
    .out0(S0), .out1(S1), .out2(S2), .out3(S3), .out4(S4), .out5(S5), .out6(S6), .out7(S7), .out8(S8),
    .out9(S9), .out10(S10), .out11(S11), .out12(S12), .out13(S13), .out14(S14), .out15(S15), .out16(S16),
    .out17(S17), .out18(S18), .out19(S19), .out20(S20), .out21(S21), .out22(S22), .out23(S23), .out24(S24),
    .out25(S25), .out26(S26), .out27(S27), .out28(S28), .out29(S29), .out30(S30), .out31(S31), .in(RegWr),
    .sel(rw));
  Register #(.width(32), .trigger("rising"), .Select("low")) Reg0 (.D(busW), .en(S0), .Q(_0), .clk(Clk), .clr(Reset));
  Register #(.width(32), .trigger("rising"), .Select("low")) Reg1 (.D(busW), .en(S1), .Q(_1), .clk(Clk), .clr(Reset));
  Register #(.width(32), .trigger("rising"), .Select("low")) Reg2 (.D(busW), .en(S2), .Q(_2), .clk(Clk), .clr(Reset));
  Register #(.width(32), .trigger("rising"), .Select("low")) Reg3 (.D(busW), .en(S3), .Q(_3), .clk(Clk), .clr(Reset));
  Register #(.width(32), .trigger("rising"), .Select("low")) Reg4 (.D(busW), .en(S4), .Q(_4), .clk(Clk), .clr(Reset));
  Register #(.width(32), .trigger("rising"), .Select("low")) Reg5 (.D(busW), .en(S5), .Q(_5), .clk(Clk), .clr(Reset));
  Register #(.width(32), .trigger("rising"), .Select("low")) Reg6 (.D(busW), .en(S6), .Q(_6), .clk(Clk), .clr(Reset));
  Register #(.width(32), .trigger("rising"), .Select("low")) Reg7 (.D(busW), .en(S7), .Q(_7), .clk(Clk), .clr(Reset));
  Multiplexer #(.select(5), .width(32), .disabled("Z"), .enable("false")) multiplexer_1 (
    .in0(_0), .in1(_1), .in2(_2), .in3(_3), .in4(_4), .in5(_5), .in6(_6), .in7(_7), .in8(_8), .in9(_9),
    .in10(_10), .in11(_11), .in12(_12), .in13(_13), .in14(_14), .in15(_15), .in16(_16), .in17(_17),
    .in18(_18), .in19(_19), .in20(_20), .in21(_21), .in22(_22), .in23(_23), .in24(_24), .in25(_25),
    .in26(_26), .in27(_27), .in28(_28), .in29(_29), .in30(_30), .in31(_31), .out(busA), .sel(ra));
  Register #(.width(32), .trigger("rising"), .Select("low")) Reg8 (.D(busW), .en(S8), .Q(_8), .clk(Clk), .clr(Reset));
  Register #(.width(32), .trigger("rising"), .Select("low")) Reg9 (.D(busW), .en(S9), .Q(_9), .clk(Clk), .clr(Reset));
  Register #(.width(32), .trigger("rising"), .Select("low")) Reg10 (
    .D(busW), .en(S10), .Q(_10), .clk(Clk), .clr(Reset));
  Register #(.width(32), .trigger("rising"), .Select("low")) Reg11 (
    .D(busW), .en(S11), .Q(_11), .clk(Clk), .clr(Reset));
  Register #(.width(32), .trigger("rising"), .Select("low")) Reg12 (
    .D(busW), .en(S12), .Q(_12), .clk(Clk), .clr(Reset));
  Register #(.width(32), .trigger("rising"), .Select("low")) Reg13 (
    .D(busW), .en(S13), .Q(_13), .clk(Clk), .clr(Reset));
  Register #(.width(32), .trigger("rising"), .Select("low")) Reg14 (
    .D(busW), .en(S14), .Q(_14), .clk(Clk), .clr(Reset));
  Register #(.width(32), .trigger("rising"), .Select("low")) Reg15 (
    .D(busW), .en(S15), .Q(_15), .clk(Clk), .clr(Reset));
  Register #(.width(32), .trigger("rising"), .Select("low")) Reg16 (
    .D(busW), .en(S16), .Q(_16), .clk(Clk), .clr(Reset));
  Register #(.width(32), .trigger("rising"), .Select("low")) Reg17 (
    .D(busW), .en(S17), .Q(_17), .clk(Clk), .clr(Reset));
  Register #(.width(32), .trigger("rising"), .Select("low")) Reg18 (
    .D(busW), .en(S18), .Q(_18), .clk(Clk), .clr(Reset));
  Register #(.width(32), .trigger("rising"), .Select("low")) Reg19 (
    .D(busW), .en(S19), .Q(_19), .clk(Clk), .clr(Reset));
  Register #(.width(32), .trigger("rising"), .Select("low")) Reg20 (
    .D(busW), .en(S20), .Q(_20), .clk(Clk), .clr(Reset));
  Register #(.width(32), .trigger("rising"), .Select("low")) Reg21 (
    .D(busW), .en(S21), .Q(_21), .clk(Clk), .clr(Reset));
  Register #(.width(32), .trigger("rising"), .Select("low")) Reg22 (
    .D(busW), .en(S22), .Q(_22), .clk(Clk), .clr(Reset));
  Register #(.width(32), .trigger("rising"), .Select("low")) Reg23 (
    .D(busW), .en(S23), .Q(_23), .clk(Clk), .clr(Reset));
  Multiplexer #(.select(5), .width(32), .disabled("Z"), .enable("false")) multiplexer_2 (
    .in0(_0), .in1(_1), .in2(_2), .in3(_3), .in4(_4), .in5(_5), .in6(_6), .in7(_7), .in8(_8), .in9(_9),
    .in10(_10), .in11(_11), .in12(_12), .in13(_13), .in14(_14), .in15(_15), .in16(_16), .in17(_17),
    .in18(_18), .in19(_19), .in20(_20), .in21(_21), .in22(_22), .in23(_23), .in24(_24), .in25(_25),
    .in26(_26), .in27(_27), .in28(_28), .in29(_29), .in30(_30), .in31(_31), .out(busB), .sel(rb));
  Register #(.width(32), .trigger("rising"), .Select("low")) Reg24 (
    .D(busW), .en(S24), .Q(_24), .clk(Clk), .clr(Reset));
  Register #(.width(32), .trigger("rising"), .Select("low")) Reg25 (
    .D(busW), .en(S25), .Q(_25), .clk(Clk), .clr(Reset));
  Register #(.width(32), .trigger("rising"), .Select("low")) Reg26 (
    .D(busW), .en(S26), .Q(_26), .clk(Clk), .clr(Reset));
  Register #(.width(32), .trigger("rising"), .Select("low")) Reg27 (
    .D(busW), .en(S27), .Q(_27), .clk(Clk), .clr(Reset));
  Register #(.width(32), .trigger("rising"), .Select("low")) Reg28 (
    .D(busW), .en(S28), .Q(_28), .clk(Clk), .clr(Reset));
  Register #(.width(32), .trigger("rising"), .Select("low")) Reg29 (
    .D(busW), .en(S29), .Q(_29), .clk(Clk), .clr(Reset));
  Register #(.width(32), .trigger("rising"), .Select("low")) Reg30 (
    .D(busW), .en(S30), .Q(_30), .clk(Clk), .clr(Reset));
  Register #(.width(32), .trigger("rising"), .Select("low")) Reg31 (
    .D(busW), .en(S31), .Q(_31), .clk(Clk), .clr(Reset));
endmodule

// 18021006 EXT
module _18021006_EXT (
  input  [15:0] Input_Imm16,
  input  [1:0] ExtOp,
  output [31:0] Output32
);

  wire [31:0] bit_extender_1_out, bit_extender_2_out;

  assign bit_extender_1_out = {{16{1'b0}}, Input_Imm16};  // Bit_Extender bit_extender_1
  assign bit_extender_2_out = {{16{Input_Imm16[15]}}, Input_Imm16};  // Bit_Extender bit_extender_2
  Multiplexer #(.select(2), .width(32), .disabled("Z"), .enable("false")) multiplexer_1 (
    .in0(bit_extender_1_out), .in1({Input_Imm16, {16{1'b0}}}), .in2(bit_extender_2_out), .out(Output32),
    .sel(ExtOp));  // open: in3
endmodule

// 18021006 DM
module _18021006_DM (
  input  Clk,
  input  MemWr,
  input  [31:0] busA,
  input  [31:0] busB,
  output [31:0] Out
);

  RAM #(.addrWidth(8), .dataWidth(8), .bus("separate"), .Select("low")) ram_1 (
    .addr(busA[9:2]), .din(busB[7:0]), .data(Out[7:0]), .str(MemWr), .clk(Clk));  // open: sel, ld, clr
  RAM #(.addrWidth(8), .dataWidth(8), .bus("separate"), .Select("low")) ram_2 (
    .addr(busA[9:2]), .din(busB[15:8]), .data(Out[15:8]), .str(MemWr), .clk(Clk));  // open: sel, ld, clr
  RAM #(.addrWidth(8), .dataWidth(8), .bus("separate"), .Select("low")) ram_3 (
    .addr(busA[9:2]), .din(busB[23:16]), .data(Out[23:16]), .str(MemWr), .clk(Clk));  // open: sel, ld, clr
  RAM #(.addrWidth(8), .dataWidth(8), .bus("separate"), .Select("low")) ram_4 (
    .addr(busA[9:2]), .din(busB[31:24]), .data(Out[31:24]), .str(MemWr), .clk(Clk));  // open: sel, ld, clr
endmodule

// 18021006 Controller
module _18021006_Controller (
  input  [5:0] opcode,
  input  [5:0] funct,
  output RegDst,
  output ALUSrc,
  output MemtoReg,
  output RegWrite,
  output MemWrite,
  output nPC_sel,
  output [1:0] Extop,
  output jsel,
  output [2:0] ALUctr
);

  wire addu_out, subu_out;

  and addu (addu_out, ~opcode[5], ~opcode[4], ~opcode[3], ~opcode[2], ~opcode[1], ~opcode[0], funct[5], ~funct[4], ~funct[3], ~funct[2], ~funct[1], funct[0]);  // AND_Gate
  and subu (subu_out, ~opcode[5], ~opcode[4], ~opcode[3], ~opcode[2], ~opcode[1], ~opcode[0], funct[5], ~funct[4], ~funct[3], ~funct[2], funct[1], funct[0]);  // AND_Gate
  and ori (ALUctr[2], ~opcode[5], ~opcode[4], opcode[3], opcode[2], ~opcode[1], opcode[0]);  // AND_Gate
  and lw (MemtoReg, opcode[5], ~opcode[4], ~opcode[3], ~opcode[2], opcode[1], opcode[0]);  // AND_Gate
  and sw (MemWrite, opcode[5], ~opcode[4], opcode[3], ~opcode[2], opcode[1], opcode[0]);  // AND_Gate
  and beq (nPC_sel, ~opcode[5], ~opcode[4], ~opcode[3], opcode[2], ~opcode[1], ~opcode[0]);  // AND_Gate
  and lui (Extop[0], ~opcode[5], ~opcode[4], opcode[3], opcode[2], opcode[1], opcode[0]);  // AND_Gate
  and j (jsel, ~opcode[5], ~opcode[4], ~opcode[3], ~opcode[2], opcode[1], ~opcode[0]);  // AND_Gate
  or or_1 (RegDst, addu_out, subu_out);
  or or_2 (ALUSrc, ALUctr[2], MemtoReg, MemWrite, Extop[0]);
  or or_3 (RegWrite, addu_out, subu_out, Extop[0], ALUctr[2], MemtoReg);
  or or_4 (Extop[1], MemtoReg, MemWrite);
  or or_5 (ALUctr[1], subu_out, nPC_sel);
  or or_6 (ALUctr[0], addu_out, MemtoReg, MemWrite);
endmodule

module _18021006_Carrier (
  input  G3_star,
  input  P3_star,
  input  G2_star,
  input  P2_star,
  input  G1_star,
  input  P1_star,
  input  G0_star,
  input  P0_star,
  input  C0,
  output G0_star_2,
  output P0_star_2,
  output C3,
  output C2,
  output C1
);

  wire and_1_out, and_2_out, and_3_out, and_4_out, and_5_out, and_6_out, and_7_out, and_8_out, and_9_out;

  and and_1 (and_1_out, P3_star, G2_star);
  and and_2 (and_2_out, P3_star, P2_star, G1_star);
  and and_3 (and_3_out, P3_star, P2_star, P1_star, G0_star);
  and and_4 (and_4_out, P2_star, G1_star);
  and and_5 (and_5_out, P2_star, P1_star, G0_star);
  and and_6 (and_6_out, P2_star, P1_star, P0_star, C0);
  and and_7 (and_7_out, P1_star, G0_star);
  and and_8 (and_8_out, P1_star, P0_star, C0);
  and and_9 (and_9_out, P0_star, C0);
  or or_1 (G0_star_2, G3_star, and_1_out, and_2_out, and_3_out);
  and and_10 (P0_star_2, P3_star, P2_star, P1_star, P0_star);
  or or_2 (C3, G2_star, and_4_out, and_5_out, and_6_out);
  or or_3 (C2, G1_star, and_7_out, and_8_out);
  or or_4 (C1, G0_star, and_9_out);
endmodule

module _18021006_Four_bit_parallel_adder (
  input  A3,
  input  B3,
  input  A2,
  input  B2,
  input  A1,
  input  B1,
  input  A0,
  input  B0,
  input  C0,
  output G0_star,
  output P0_star,
  output _3,
  output _2,
  output \Σ1 ,
  output _0
);

  wire and_1_out, and_2_out, and_3_out, and_4_out, and_5_out, and_6_out, and_7_out, and_8_out, and_9_out,
       G0_out, G1_out, G2_out, G3_out, or_2_out, or_3_out, or_4_out, P0_out, P1_out, P2_out, P3_out;

  and G3 (G3_out, A3, B3);
  xor P3 (P3_out, A3, B3);
  and G2 (G2_out, A2, B2);
  xor P2 (P2_out, A2, B2);
  and G1 (G1_out, A1, B1);
  xor P1 (P1_out, A1, B1);
  and G0 (G0_out, A0, B0);
  xor P0 (P0_out, A0, B0);
  and and_1 (and_1_out, P3_out, G2_out);
  and and_2 (and_2_out, P3_out, P2_out, G1_out);
  and and_3 (and_3_out, P3_out, P2_out, P1_out, G0_out);
  and and_4 (and_4_out, P2_out, G1_out);
  and and_5 (and_5_out, P2_out, P1_out, G0_out);
  and and_6 (and_6_out, P2_out, P1_out, P0_out, C0);
  and and_7 (and_7_out, P1_out, G0_out);
  and and_8 (and_8_out, P1_out, P0_out, C0);
  and and_9 (and_9_out, P0_out, C0);
  or or_1 (G0_star, G3_out, and_1_out, and_2_out, and_3_out);
  and and_10 (P0_star, P3_out, P2_out, P1_out, P0_out);
  or or_2 (or_2_out, G2_out, and_4_out, and_5_out, and_6_out);
  or or_3 (or_3_out, G1_out, and_7_out, and_8_out);
  or or_4 (or_4_out, G0_out, and_9_out);
  xor xor_1 (_3, P3_out, or_2_out);
  xor xor_2 (_2, P2_out, or_3_out);
  xor xor_3 (\Σ1 , P1_out, or_4_out);
  xor xor_4 (_0, P0_out, C0);
endmodule

// 18021006 ALU
module _18021006_ALU (
  input  [31:0] busA,
  input  [31:0] busB,
  input  [2:0] ALUctr,
  output zero,
  output [31:0] out
);

  wire [31:0] n18021006_32bit_parallel_adder_1_out_4, n18021006_32bit_parallel_adder_2_out_4,
       n18021006_32bit_parallel_adder_3_out_4, not_1_out, ori_out;

  assign not_1_out = ~busB;  // NOT_Gate not_1, 32 bits wide
  _18021006_32bit_parallel_adder u_18021006_32bit_parallel_adder_1 (
    .busA(not_1_out), .busB(32'h1), .C0(1'b0), .out_4(n18021006_32bit_parallel_adder_1_out_4));
  nor nor_1 (zero, n18021006_32bit_parallel_adder_3_out_4[31], n18021006_32bit_parallel_adder_3_out_4[30], n18021006_32bit_parallel_adder_3_out_4[29], n18021006_32bit_parallel_adder_3_out_4[28], n18021006_32bit_parallel_adder_3_out_4[27], n18021006_32bit_parallel_adder_3_out_4[26], n18021006_32bit_parallel_adder_3_out_4[25], n18021006_32bit_parallel_adder_3_out_4[24], n18021006_32bit_parallel_adder_3_out_4[23], n18021006_32bit_parallel_adder_3_out_4[22], n18021006_32bit_parallel_adder_3_out_4[21], n18021006_32bit_parallel_adder_3_out_4[20], n18021006_32bit_parallel_adder_3_out_4[19], n18021006_32bit_parallel_adder_3_out_4[18], n18021006_32bit_parallel_adder_3_out_4[17], n18021006_32bit_parallel_adder_3_out_4[16], n18021006_32bit_parallel_adder_3_out_4[14], n18021006_32bit_parallel_adder_3_out_4[13], n18021006_32bit_parallel_adder_3_out_4[12], n18021006_32bit_parallel_adder_3_out_4[11], n18021006_32bit_parallel_adder_3_out_4[10], n18021006_32bit_parallel_adder_3_out_4[9], n18021006_32bit_parallel_adder_3_out_4[8], n18021006_32bit_parallel_adder_3_out_4[7], n18021006_32bit_parallel_adder_3_out_4[6], n18021006_32bit_parallel_adder_3_out_4[5], n18021006_32bit_parallel_adder_3_out_4[4], n18021006_32bit_parallel_adder_3_out_4[3], n18021006_32bit_parallel_adder_3_out_4[2], n18021006_32bit_parallel_adder_3_out_4[1], n18021006_32bit_parallel_adder_3_out_4[0], n18021006_32bit_parallel_adder_3_out_4[15]);
  _18021006_32bit_parallel_adder u_18021006_32bit_parallel_adder_2 (
    .busA(busA), .busB(busB), .C0(1'b0), .out_4(n18021006_32bit_parallel_adder_2_out_4));
  _18021006_32bit_parallel_adder u_18021006_32bit_parallel_adder_3 (
    .busA(busA), .busB(n18021006_32bit_parallel_adder_1_out_4), .C0(1'b0),
    .out_4(n18021006_32bit_parallel_adder_3_out_4));
  assign ori_out = busA | busB;  // OR_Gate ori, 32 bits wide
  Multiplexer #(.select(3), .width(32), .disabled("Z"), .enable("false")) multiplexer_1 (
    .in0(busB), .in1(n18021006_32bit_parallel_adder_2_out_4), .in2(n18021006_32bit_parallel_adder_3_out_4),
    .in4(ori_out), .out(out), .sel(ALUctr));  // open: in3, in5, in6, in7
endmodule

module _18021006_16bit_parallel_adder (
  input  A15,
  input  B15,
  input  A14,
  input  B14,
  input  A13,
  input  B13,
  input  A12,
  input  B12,
  input  A11,
  input  B11,
  input  A10,
  input  B10,
  input  A9,
  input  B9,
  input  A8,
  input  B8,
  input  A7,
  input  B7,
  input  C0,
  input  A6,
  input  B6,
  input  A5,
  input  B5,
  input  A4,
  input  B4,
  input  A3,
  input  B3,
  input  A2,
  input  B2,
  input  A1,
  input  B1,
  input  A0,
  input  B0,
  output G_star,
  output P_star,
  output \Σ15 ,
  output \Σ14 ,
  output \Σ13 ,
  output \Σ12 ,
  output \Σ11 ,
  output \Σ10 ,
  output \Σ9 ,
  output \Σ8 ,
  output \Σ7 ,
  output \Σ6 ,
  output \Σ5 ,
  output \Σ4 ,
  output \Σ3 ,
  output \Σ2 ,
  output \Σ1 ,
  output \Σ0 
);

  wire C4, C8, C12, G0_star, G1_star, G2_star, G3_star, P0_star, P1_star, P2_star, P3_star;

  _18021006_Four_bit_parallel_adder u_18021006_four_bit_parallel_adder_1 (
    .A3(A15), .B3(B15), .A2(A14), .B2(B14), .A1(A13), .B1(B13), .A0(A12), .B0(B12), .C0(C12),
    .G0_star(G3_star), .P0_star(P3_star), ._3(\Σ15 ), ._2(\Σ14 ), .\Σ1 (\Σ13 ), ._0(\Σ12 ));
  _18021006_Four_bit_parallel_adder u_18021006_four_bit_parallel_adder_2 (
    .A3(A11), .B3(B11), .A2(A10), .B2(B10), .A1(A9), .B1(B9), .A0(A8), .B0(B8), .C0(C8), .G0_star(G2_star),
    .P0_star(P2_star), ._3(\Σ11 ), ._2(\Σ10 ), .\Σ1 (\Σ9 ), ._0(\Σ8 ));
  _18021006_Four_bit_parallel_adder u_18021006_four_bit_parallel_adder_3 (
    .A3(A7), .B3(B7), .A2(A6), .B2(B6), .A1(A5), .B1(B5), .A0(A4), .B0(B4), .C0(C4), .G0_star(G1_star),
    .P0_star(P1_star), ._3(\Σ7 ), ._2(\Σ6 ), .\Σ1 (\Σ5 ), ._0(\Σ4 ));
  _18021006_Four_bit_parallel_adder u_18021006_four_bit_parallel_adder_4 (
    .A3(A3), .B3(B3), .A2(A2), .B2(B2), .A1(A1), .B1(B1), .A0(A0), .B0(B0), .C0(C0), .G0_star(G0_star),
    .P0_star(P0_star), ._3(\Σ3 ), ._2(\Σ2 ), .\Σ1 (\Σ1 ), ._0(\Σ0 ));
  _18021006_Carrier u_18021006_carrier_1 (
    .G3_star(G3_star), .P3_star(P3_star), .G2_star(G2_star), .P2_star(P2_star), .G1_star(G1_star),
    .P1_star(P1_star), .G0_star(G0_star), .P0_star(P0_star), .C0(C0), .G0_star_2(G_star), .P0_star_2(P_star),
    .C3(C12), .C2(C8), .C1(C4));
endmodule

// Add
module _18021006_32bit_parallel_adder (
  input  [31:0] busA,
  input  [31:0] busB,
  input  C0,
  output [31:0] out_4
);

  wire C16, G_star, n18021006_16bit_parallel_adder_2_g_star, n18021006_16bit_parallel_adder_2_p_star, P_star;

  _18021006_16bit_parallel_adder u_18021006_16bit_parallel_adder_1 (
    .A15(busA[31]), .B15(busB[31]), .A14(busA[30]), .B14(busB[30]), .A13(busA[29]), .B13(busB[29]),
    .A12(busA[28]), .B12(busB[28]), .A11(busA[27]), .B11(busB[27]), .A10(busA[26]), .B10(busB[26]),
    .A9(busA[25]), .B9(busB[25]), .A8(busA[24]), .B8(busB[24]), .A7(busA[23]), .B7(busB[23]), .A6(busA[22]),
    .B6(busB[22]), .A5(busA[21]), .B5(busB[21]), .A4(busA[20]), .B4(busB[20]), .A3(busA[19]), .B3(busB[19]),
    .A2(busA[18]), .B2(busB[18]), .A1(busA[17]), .B1(busB[17]), .A0(busA[16]), .B0(busB[16]), .C0(C16),
    .G_star(G_star), .P_star(P_star), .\Σ15 (out_4[31]), .\Σ14 (out_4[30]), .\Σ13 (out_4[29]),
    .\Σ12 (out_4[28]), .\Σ11 (out_4[27]), .\Σ10 (out_4[26]), .\Σ9 (out_4[25]), .\Σ8 (out_4[24]),
    .\Σ7 (out_4[23]), .\Σ6 (out_4[22]), .\Σ5 (out_4[21]), .\Σ4 (out_4[20]), .\Σ3 (out_4[19]),
    .\Σ2 (out_4[18]), .\Σ1 (out_4[17]), .\Σ0 (out_4[16]));
  _18021006_16bit_parallel_adder u_18021006_16bit_parallel_adder_2 (
    .A15(busA[15]), .B15(busB[15]), .A14(busA[14]), .B14(busB[14]), .A13(busA[13]), .B13(busB[13]),
    .A12(busA[12]), .B12(busB[12]), .A11(busA[11]), .B11(busB[11]), .A10(busA[10]), .B10(busB[10]),
    .A9(busA[9]), .B9(busB[9]), .A8(busA[8]), .B8(busB[8]), .A7(busA[7]), .B7(busB[7]), .A6(busA[6]),
    .B6(busB[6]), .A5(busA[5]), .B5(busB[5]), .A4(busA[4]), .B4(busB[4]), .A3(busA[3]), .B3(busB[3]),
    .A2(busA[2]), .B2(busB[2]), .A1(busA[1]), .B1(busB[1]), .A0(busA[0]), .B0(busB[0]), .C0(C0),
    .G_star(n18021006_16bit_parallel_adder_2_g_star), .P_star(n18021006_16bit_parallel_adder_2_p_star),
    .\Σ15 (out_4[15]), .\Σ14 (out_4[14]), .\Σ13 (out_4[13]), .\Σ12 (out_4[12]), .\Σ11 (out_4[11]),
    .\Σ10 (out_4[10]), .\Σ9 (out_4[9]), .\Σ8 (out_4[8]), .\Σ7 (out_4[7]), .\Σ6 (out_4[6]), .\Σ5 (out_4[5]),
    .\Σ4 (out_4[4]), .\Σ3 (out_4[3]), .\Σ2 (out_4[2]), .\Σ1 (out_4[1]), .\Σ0 (out_4[0]));
  _18021006_Carrier u_18021006_carrier_1 (
    .G1_star(G_star), .P1_star(P_star), .G0_star(n18021006_16bit_parallel_adder_2_g_star),
    .P0_star(n18021006_16bit_parallel_adder_2_p_star), .C0(C0), .C1(C16));  // open: G3_star, P3_star, G2_star, P2_star, G0_star_2, P0_star_2, C3, C2

  // Other names for the same wires on the sheet: A0 = busA[0]; A1 = busA[1]; A2 = busA[2]; A3 = busA[3]; A4 = busA[4];
  //   A5 = busA[5]; A6 = busA[6]; A7 = busA[7]; A8 = busA[8]; A9 = busA[9]; A10 = busA[10]; A11 = busA[11];
  //   A12 = busA[12]; A13 = busA[13]; A14 = busA[14]; A15 = busA[15]; A16 = busA[16]; A17 = busA[17]; A18 = busA[18];
  //   A19 = busA[19]; A20 = busA[20]; A21 = busA[21]; A22 = busA[22]; A23 = busA[23]; A24 = busA[24]; A25 = busA[25];
  //   A26 = busA[26]; A27 = busA[27]; A28 = busA[28]; A29 = busA[29]; A30 = busA[30]; A31 = busA[31]; B0 = busB[0];
  //   B1 = busB[1]; B2 = busB[2]; B3 = busB[3]; B4 = busB[4]; B5 = busB[5]; B6 = busB[6]; B7 = busB[7]; B8 = busB[8];
  //   B9 = busB[9]; B10 = busB[10]; B11 = busB[11]; B12 = busB[12]; B13 = busB[13]; B14 = busB[14]; B15 = busB[15];
  //   B16 = busB[16]; B17 = busB[17]; B18 = busB[18]; B19 = busB[19]; B20 = busB[20]; B21 = busB[21]; B22 = busB[22];
  //   B23 = busB[23]; B24 = busB[24]; B25 = busB[25]; B26 = busB[26]; B27 = busB[27]; B28 = busB[28]; B29 = busB[29];
  //   B30 = busB[30]; B31 = busB[31]
endmodule
